# Fritzing sketch Estufa (saved by Fritzing 1.0.4)
circuit board: 8.46667cm x 5.64444cm
breadboards: 1

parts:
  Mod1 = Amica NodeMCU DEVKIT 1.0
  R1 = Photocell (LDR) [power=0.25W dark_resistance_@0.01lx=300kΩ light_resistance_@100lx=400Ω luminance=10lx package=THT]
  R2 = Resistor [tolerance=±5% resistance=10k package="0805 [SMD]"]
  4501_Multiplexer = 74HC4051 [package=so16]
  Part1 = FC-28 Soil Hygrometer Module
  부품2 = FC-28 Soil Hygrometer Module - Probe
  DHT11 = Humidity and Temperature Sensor RHT03
  Grove1 = Grove OLED 128x96
  KY-1 = Keyes Relay [package=THT]
  KY-2 = Keyes Relay [package=THT]
  KY-3 = Keyes Relay [package=THT]

nets:
  VCC: Mod1.pin1, Mod1.pin_10, Mod1.pin_26, R2.Pin_1, 4501_Multiplexer.VDD, Part1.VCC, DHT11.Vcc, Grove1.VCC, KY-1.power, KY-2.power, KY-3.power
  GND: Mod1.pin2, Mod1.pin_9, Mod1.pin_25, Mod1.pin_29, R1.pin_0, 4501_Multiplexer.INH, 4501_Multiplexer.VEE, 4501_Multiplexer.VSS, Part1.GND, DHT11.GND_2, Grove1.GND, KY-1.ground, KY-2.ground, KY-3.ground
  N1: Mod1.pin5, 4501_Multiplexer.C
  N2: Mod1.pin6, 4501_Multiplexer.B
  N3: Mod1.pin8, KY-3.signal
  N4: Mod1.pin_11, KY-2.signal
  N5: Mod1.pin_12, KY-1.signal
  N6: Mod1.pin_13, Grove1.SDA
  N7: Mod1.pin_14, Grove1.SCL
  N8: Mod1.pin_15, 4501_Multiplexer.A
  N9: Mod1.pin_16, 4501_Multiplexer.IO
  N10: Mod1.pin_19, Part1.DO
  N11: R1.pin_1, R2.Pin_0, 4501_Multiplexer.IO1
  N12: 4501_Multiplexer.IO0, Part1.AO
  N13: 4501_Multiplexer.IO2, DHT11.Data-signal
  N14: Part1.POS, 부품2.POS
  N15: Part1.NEG, 부품2.NEG

notes:
  SD3-GPIO 10
  R1 - LAMPAD
  R2 - ESTUFA
  R3 - AGUA
  NC = Normal Closed
  C = Closed
  NO = Normal Open
  127V
  10k

custom parts:
  FC-28 Soil Hygrometer Module: The FC-28 is a soil hygrometer module that uses the Texas Instruments LM393 comparator chip to provide an analog measurement of soil humidity. The digital output is high when soil moisture is over a certain threshold, as determined by adjusting the potentiometer.
  FC-28 Soil Hygrometer Module - Probe: The FC-28 is a soil hygrometer module that uses the Texas Instruments LM393 comparator chip to provide an analog measurement of soil humidity.
  Keyes Relay: The Keyes 5V relay module is suitable for SCM development, home appliance control. It uses a 5V~12V TIL control signal which can control DC / AC signal.
